// Logisim project mhl_cpu_zero_09.circ as structural Verilog
module hex_display_8_bit (
  input  in0,
  input  in1,
  input  in2,
  input  in3,
  input  in4,
  input  in5,
  input  in6,
  input  in7
);

  wire demultiplexer_1_p2, demultiplexer_1_p3, demultiplexer_1_p4, multiplexer_1_p6, multiplexer_1_p7,
       n7_segment_display_1_p1, n7_segment_display_1_p3;

  // Multiplexer #(.select(1), .width(4)) multiplexer_1: pin names not known; wires that end beside it: in1, in2, in3, in4, in5, multiplexer_1_p6, multiplexer_1_p7
  // ROM #(.addrWidth(4), .dataWidth(8)) rom_1: pin names not known; wires that end beside it: in2, in3, in4, in5, multiplexer_1_p6, multiplexer_1_p7
  // Demultiplexer #(.select(1), .width(8)) demultiplexer_1: pin names not known; wires that end beside it: multiplexer_1_p6, demultiplexer_1_p2, demultiplexer_1_p3, demultiplexer_1_p4
  // _7_Segment_Display 7_segment_display_1: pin names not known; wires that end beside it: n7_segment_display_1_p1, demultiplexer_1_p4, n7_segment_display_1_p3
  // Splitter splitter_1: pin names not known; wires that end beside it: demultiplexer_1_p2, demultiplexer_1_p3, n7_segment_display_1_p1
  _7_Segment_Display u_7_segment_display_2 (.g(n7_segment_display_1_p3));  // open: f, a, b, e, d, c, dp
  // Splitter splitter_2: pin names not known
endmodule

module progam_counter (
  input  VCC,
  input  GND,
  input  INCREMENT,
  input  CLK,
  input  RST,
  input  LOAD,
  input  [7:0] I,
  output [7:0] _0,
  output OVERFLOW
);

  wire splitter_1_p2, splitter_1_p4, splitter_1_p6, splitter_1_p8, splitter_1_p11, splitter_1_p13,
       splitter_1_p15, splitter_1_p17, splitter_2_p3, splitter_2_p5, splitter_2_p7, splitter_2_p9,
       splitter_2_p12, splitter_2_p14, splitter_2_p16, splitter_2_p18;

  // NOT_Gate not_1 has open pins: in=RST, out=open
  _74161 MSB (.pin9(VCC));  // open: pin1, pin2, pin3, pin4, pin5, pin6, pin7, pin15, pin14, pin13, pin12, pin11, pin10
  // Splitter splitter_1: pin names not known; wires that end beside it: CLK, splitter_1_p2, splitter_1_p2, splitter_1_p4, splitter_1_p4, splitter_1_p6, splitter_1_p6, splitter_1_p8, splitter_1_p8, _0, splitter_1_p11, splitter_1_p11, splitter_1_p13, splitter_1_p13, splitter_1_p15, splitter_1_p15, splitter_1_p17, splitter_1_p17
  // Splitter splitter_2: pin names not known; wires that end beside it: OVERFLOW, GND, splitter_2_p3, splitter_2_p3, splitter_2_p5, splitter_2_p5, splitter_2_p7, splitter_2_p7, splitter_2_p9, splitter_2_p9, I, splitter_2_p12, splitter_2_p12, splitter_2_p14, splitter_2_p14, splitter_2_p16, splitter_2_p16, splitter_2_p18, splitter_2_p18, LOAD
  // _74161 LSB: pin names not known; wires that end beside it: CLK, VCC
endmodule

module hex_led_16bit (
  input  CLK,
  input  [7:0] I,
  input  WE,
  input  MSB,
  input  RST,
  input  DISP_CLK,
  input  VCC,
  input  GND
);

  wire _00_p1, _00_p2, _00_p3, _00_p4, _03_p2, _03_p3, _03_p4, undriven_2;
  wire [7:0] LSB_BUF_p3, LSB_BUF_p4, multiplexer_1_out, undriven;

  // AND_Gate and_1 is placed but not wired
  // Register #(.width(8)) LSB_BUF: pin names not known; wires that end beside it: I, I, LSB_BUF_p3, LSB_BUF_p4
  // Register #(.width(8)) MSB_BUF: pin names not known; wires that end beside it: I, LSB_BUF_p4
  Multiplexer #(.select(1), .width(8)) multiplexer_1 (
    .in0(LSB_BUF_p3), .in1(LSB_BUF_p4), .out(multiplexer_1_out));  // open: sel
  // ROM #(.addrWidth(8), .dataWidth(8)) EEPROM: pin names not known; wires that end beside it: LSB_BUF_p3, LSB_BUF_p4, multiplexer_1_out
  Counter #(.max('hf), .width(4)) CTR2 ();  // open: clr, load, up, count, clk, D, carry, Q
  // _7_Segment_Display _00: pin names not known; wires that end beside it: _00_p1, _00_p2, _00_p3, _00_p4
  _7_Segment_Display _01 (.g(_00_p2), .b(_00_p4), .e(_00_p3), .dp(undriven_2));  // open: f, a, d, c
  _7_Segment_Display _02 (.g(_00_p4), .b(_03_p3), .e(undriven_2), .dp(_03_p4));  // open: f, a, d, c
  Demultiplexer #(.select(2), .width(8)) demultiplexer_1 (.in(undriven));  // open: out0, out1, out2, out3, sel
  // _7_Segment_Display _03: pin names not known; wires that end beside it: _00_p4, _03_p2, _03_p3, _03_p4
endmodule
